// Logisim project tt.circ as structural Verilog: 5 circuits, main circuit main
module main (
);

  wire add_1_out_3, add_1_out_4, dipswitch_1_p1, dipswitch_1_p2, dipswitch_1_p3, not_1_out, not_2_out,
       or_1_out, or_2_out, transistor_1_out, transistor_2_out, transistorn_1_out_3, transistorn_2_out_3;

  // DipSwitch #(.number(3)) dipswitch_1: pin names not known; wires that end beside it: dipswitch_1_p1, dipswitch_1_p2, dipswitch_1_p3, dipswitch_1_p1, dipswitch_1_p2, dipswitch_1_p1
  Transistor transistor_1 (.in(dipswitch_1_p2), .out(transistor_1_out), .gate(dipswitch_1_p1));
  Transistor transistor_2 (.in(dipswitch_1_p3), .out(transistor_2_out), .gate(dipswitch_1_p1));
  TransistorN transistorn_1 (.in_2(dipswitch_1_p2), .in_1(dipswitch_1_p1), .out_3(transistorn_1_out_3));
  TransistorN transistorn_2 (.in_2(dipswitch_1_p3), .in_1(dipswitch_1_p1), .out_3(transistorn_2_out_3));
  not not_1 (not_1_out, transistor_1_out);
  not not_2 (not_2_out, transistor_2_out);
  or or_1 (or_1_out, transistorn_1_out_3, not_1_out);
  or or_2 (or_2_out, transistorn_2_out_3, not_2_out);
  LED led_1 (.in(add_1_out_3));
  ADD add_1 (.in_1(or_1_out), .in_2(or_2_out), .out_3(add_1_out_3), .out_4(add_1_out_4));
  LED led_2 (.in(add_1_out_4));
endmodule

module ADD (
  input  in_1,
  input  in_2,
  output out_3,
  output out_4
);

  wire nand_1_out, or_1_out;

  and and_1 (out_4, in_1, in_2);
  or or_1 (or_1_out, in_1, in_2);
  nand nand_1 (nand_1_out, or_1_out, out_4);
  and and_2 (out_3, nand_1_out, or_1_out);
endmodule

module MPD (
  input  in_1,
  input  in_2,
  input  in_3,
  output out_4,
  output out_5,
  output out_6,
  output out_7
);

  Transistor transistor_1 (.in(in_2), .out(out_6), .gate(in_1));
  Transistor transistor_2 (.in(in_3), .out(out_7), .gate(in_1));
  TransistorN transistorn_1 (.in_2(in_2), .in_1(in_1), .out_3(out_4));
  TransistorN transistorn_2 (.in_2(in_3), .in_1(in_1), .out_3(out_5));
endmodule

module TransistorN (
  input  in_1,
  input  in_2,
  output out_3
);

  and and_1 (out_3, in_1, in_2);
endmodule

module MSW (
  input  in_1,
  input  in_2,
  output out_3,
  output out_4
);

  not not_1 (out_3, in_1);
  not not_2 (out_4, in_2);
endmodule
